// Logisim project DeMorgan.circ as structural Verilog: 1 circuit, main circuit main
module main (
  input  A,
  input  A_2,
  input  B,
  input  B_2,
  input  A_3,
  input  A_4,
  input  B_3,
  input  B_4,
  output F,
  output F_2,
  output F_3,
  output F_4
);

  nand nand_1 (F, A, B);
  nor nor_1 (F_3, A_3, B_3);
  or or_1 (F_2, ~A_2, ~B_2);  // OR_Gate
  and and_1 (F_4, ~A_4, ~B_4);  // AND_Gate
endmodule
