// Logisim project Introdução.circ as structural Verilog: 1 circuit, main circuit main
module main (
  input  X,
  input  X_2,
  input  X_3,
  input  X_4,
  input  X_5,
  input  X_6,
  input  X_7,
  input  X_8,
  output _0,
  output X_9,
  output X_10,
  output X_11,
  output X_12,
  output X_13,
  output _0_2,
  output _1
);

  wire not_1_out, not_2_out;

  and and_1 (_0, X, 1'b0);
  and and_2 (X_10, X_3, 1'b1);
  and and_3 (X_12, X_5, X_5);
  and and_4 (_0_2, X_7, not_1_out);
  not not_1 (not_1_out, X_7);
  not not_2 (not_2_out, X_8);
  or or_1 (X_9, X_2, 1'b0);
  or or_2 (X_11, X_4, 1'b1);
  or or_3 (X_13, X_6, X_6);
  or or_4 (_1, X_8, not_2_out);
endmodule
