// Logisim project DE0-CV_ITA.circ as structural Verilog: 1 circuit, main circuit main
module main (
  input  CLK,
  output out_2,
  output out_3,
  output out_4,
  output out_5,
  output out_6,
  output out_7,
  output out_8,
  output out_9
);

  wire and_1_out, and_2_out, and_3_out, and_4_out, and_5_out, and_6_out;

  T_Flip_Flop t_ff_1 (.clk(1'b1), .T(CLK), .Q(out_2));  // open: Qn, preset, reset
  T_Flip_Flop t_ff_2 (.T(out_2), .Q(out_3));  // open: clk, Qn, preset, reset
  T_Flip_Flop t_ff_3 (.T(and_1_out), .Q(out_4));  // open: clk, Qn, preset, reset
  and and_1 (and_1_out, out_3, out_2);
  and and_2 (and_2_out, out_4, and_1_out);
  T_Flip_Flop t_ff_4 (.T(and_2_out), .Q(out_5));  // open: clk, Qn, preset, reset
  T_Flip_Flop t_ff_5 (.T(and_3_out), .Q(out_6));  // open: clk, Qn, preset, reset
  and and_3 (and_3_out, out_5, and_2_out);
  and and_4 (and_4_out, out_6, and_3_out);
  T_Flip_Flop t_ff_6 (.T(and_4_out), .Q(out_7));  // open: clk, Qn, preset, reset
  T_Flip_Flop t_ff_7 (.T(and_5_out), .Q(out_8));  // open: clk, Qn, preset, reset
  and and_5 (and_5_out, out_7, and_4_out);
  and and_6 (and_6_out, out_8, and_5_out);
  T_Flip_Flop t_ff_8 (.T(and_6_out), .Q(out_9));  // open: clk, Qn, preset, reset
endmodule
