// Logisim project Primitivas.circ as structural Verilog: 1 circuit, main circuit main
module main (
  input  A,
  input  A_2,
  input  A_3,
  input  A_4,
  input  B,
  input  B_2,
  input  A_5,
  input  A_6,
  input  B_3,
  input  B_4,
  output F,
  output F_2,
  output F_3,
  output F_4,
  output F_5,
  output F_6
);

  wire nand_2_out, nand_3_out, nand_4_out;

  nand nand_1 (F, A, A);
  nand nand_2 (nand_2_out, A_3, B);
  nand nand_3 (nand_3_out, A_5, A_5);
  nand nand_4 (nand_4_out, B_4, B_4);
  nand nand_5 (F_3, nand_2_out, nand_2_out);
  nand nand_6 (F_5, nand_3_out, nand_4_out);
  not not_1 (F_2, A_2);
  and and_1 (F_4, A_4, B_2);
  or or_1 (F_6, A_6, B_3);
endmodule
