// Logisim project DE0-CV.circ as structural Verilog: 1 circuit, main circuit main
module main (
  input  CLK,
  output out_2,
  output out_3,
  output out_4,
  output out_5,
  output out_6,
  output out_7,
  output out_8,
  output out_9
);

  wire and_1_out, and_2_out, and_3_out, and_4_out, and_5_out, and_6_out;

  T_Flip_Flop t_ff_1 (.clk(CLK), .T(1'b1), .Q(out_2), .reset(1'b0));  // open: Qn, preset
  T_Flip_Flop t_ff_2 (.clk(CLK), .T(out_2), .Q(out_3), .reset(1'b0));  // open: Qn, preset
  T_Flip_Flop t_ff_3 (.clk(CLK), .T(and_1_out), .Q(out_4), .reset(1'b0));  // open: Qn, preset
  and and_1 (and_1_out, out_3, out_2);
  and and_2 (and_2_out, out_4, and_1_out);
  T_Flip_Flop t_ff_4 (.clk(CLK), .T(and_2_out), .Q(out_5), .reset(1'b0));  // open: Qn, preset
  T_Flip_Flop t_ff_5 (.clk(CLK), .T(and_3_out), .Q(out_6), .reset(1'b0));  // open: Qn, preset
  and and_3 (and_3_out, out_5, and_2_out);
  and and_4 (and_4_out, out_6, and_3_out);
  T_Flip_Flop t_ff_6 (.clk(CLK), .T(and_4_out), .Q(out_7), .reset(1'b0));  // open: Qn, preset
  T_Flip_Flop t_ff_7 (.clk(CLK), .T(and_5_out), .Q(out_8), .reset(1'b0));  // open: Qn, preset
  and and_5 (and_5_out, out_7, and_4_out);
  and and_6 (and_6_out, out_8, and_5_out);
  T_Flip_Flop t_ff_8 (.clk(CLK), .T(and_6_out), .Q(out_9), .reset(1'b0));  // open: Qn, preset
endmodule
