// Logisim project contador.circ as structural Verilog: 6 circuits, main circuit main
module main (
  input  in_1,
  output [1:0] out_2,
  output [3:0] out_3,
  output [3:0] out_4,
  output [3:0] out_5,
  output [3:0] out_6,
  output [3:0] out_7,
  output [3:0] out_8,
  output [3:0] out_9
);

  wire and_1_out, and_2_out, K0, K1, K2, K3, L8, L9, not_1_out, not_2_out, or_1_out, Register_Reset, Rg1_CLK,
       Rg2_CLK, S0, S1, S2, S3, S4, S5, S6, S7, S8, S9, ULA_STATE;
  wire [1:0] HEX4;
  wire [3:0] _1out, _2out, Disp, HEX5;
  wire [7:0] contador;

  Hex_Digit_Display hex_digit_display_1 (.value(HEX5));  // open: dp
  Hex_Digit_Display hex_digit_display_2 (.value({out_2, HEX4}));  // open: dp
  LED L7 (.in(contador[7]));
  LED u_L9 (.in(L9));
  LED u_L8 (.in(L8));
  // DipSwitch #(.NSwitches(1)) S7: pin names not known; wires that end beside it: S7
  // DipSwitch #(.NSwitches(1)) S8: pin names not known; wires that end beside it: S8
  Clock clock_1 (.out(S9));
  Contador_de_Memoria contador_de_memoria_1 (
    .CLK(S9), .CLR(S0), .out_9(contador[0]), .out_10(contador[1]), .out_11(contador[2]),
    .out_12(contador[3]), .out_13(contador[4]), .out_14(contador[5]), .out_15(contador[6]),
    .out_16(contador[7]), .RgTO(HEX5[3:2]), .RgIN(HEX5[1:0]), .JMP(HEX4), .ULA(out_2), .\Disponível (Disp),
    .Operando(out_3), .Reset_Registers(Register_Reset), .ULA_State(ULA_STATE));
  // Digital_Oscilloscope digital_oscilloscope_1: pin names not known; wires that end beside it: S9, contador[0], contador[1], contador[2], contador[3], contador[4], contador[5], contador[6], contador[7], S0
  Hex_Digit_Display hex_digit_display_3 (.value(Disp));  // open: dp
  LED L4 (.in(contador[4]));
  LED L6 (.in(contador[6]));
  LED L5 (.in(contador[5]));
  // DipSwitch #(.NSwitches(1)) S6: pin names not known; wires that end beside it: S6
  // DipSwitch #(.NSwitches(1)) S4: pin names not known; wires that end beside it: S4
  // DipSwitch #(.NSwitches(1)) S5: pin names not known; wires that end beside it: S5
  Hex_Digit_Display hex_digit_display_4 (.value(_1out));  // open: dp
  Hex_Digit_Display hex_digit_display_5 (.value(out_3));  // open: dp
  LED L2 (.in(contador[2]));
  LED L3 (.in(contador[3]));
  // DipSwitch #(.NSwitches(1)) S3: pin names not known; wires that end beside it: S3
  // DipSwitch #(.NSwitches(1)) S1: pin names not known; wires that end beside it: S1
  // DipSwitch #(.NSwitches(1)) S2: pin names not known; wires that end beside it: S2
  Hex_Digit_Display hex_digit_display_6 (.value(_2out));  // open: dp
  LED L0 (.in(contador[0]));
  LED L1 (.in(contador[1]));
  // DipSwitch #(.NSwitches(1)) S0: pin names not known; wires that end beside it: S0
  Button u_K3 (.out(K3));
  Button u_K1 (.out(K1));
  Button u_K2 (.out(K2));
  Button u_K0 (.out(K0));
  Music music_1 (.in_2(in_1), .Disp(Disp));
  Adder #(.width(4)) adder_1 (.a(out_5), .b(out_3), .out(out_6));  // open: cin, cout
  Multiplier #(.width(4)) multiplier_1 (.a(out_3), .b(4'b0010), .out(out_7));  // open: cin, cout
  Subtractor #(.width(4)) subtractor_1 (.a(out_5), .b(out_3), .out(out_8));  // open: bin, bout
  Divider #(.width(4)) divider_1 (.a(out_3), .b(4'b0010), .out(out_9));  // open: upper, rem
  Multiplexer #(.select(2), .width(4), .enable("false")) multiplexer_1 (
    .in0(out_6), .in1(out_7), .in2(out_8), .in3(out_9), .out(out_4), .sel(out_2));
  Register #(.width(4), .Select("low")) Rg_1 (.D(out_4), .Q(_1out), .clk(Rg1_CLK), .clr(or_1_out));  // open: en
  Register #(.width(4), .Select("low")) Rg_2 (.D(out_4), .Q(_2out), .clk(Rg2_CLK), .clr(or_1_out));  // open: en
  Rg_IN_Multiplexer rg_in_multiplexer_1 (.in_1(HEX5[1:0]), .in_2(_1out), .in_3(_2out), .out_4(out_5));
  or or_1 (or_1_out, Register_Reset, S0);
  not not_1 (not_1_out, HEX5[3]);
  and and_1 (and_1_out, not_1_out, HEX5[2]);
  and and_2 (and_2_out, HEX5[3], not_2_out);
  not not_2 (not_2_out, HEX5[2]);
  and and_3 (Rg1_CLK, S9, ULA_STATE, and_1_out);
  and and_4 (Rg2_CLK, S9, ULA_STATE, and_2_out);

  // Other names for the same wires on the sheet: _1in[3:0] = out_4; _2in[3:0] = out_4; L0 = contador[0];
  //   L1 = contador[1]; L2 = contador[2]; L3 = contador[3]; L4 = contador[4]; L5 = contador[5]; L6 = contador[6];
  //   L7 = contador[7]; HEX0[3:0] = _2out; HEX1[3:0] = _1out; HEX3[3:0] = Disp; HEX4[3:2] = out_2;
  //   ULA_Option[1:0] = out_2; RgIN[1:0] = HEX5[1:0]; RgTO[1:0] = HEX5[3:2]; HEX2[3:0] = out_3; Operando[3:0] = out_3;
  //   Rg_IN_Value[3:0] = out_5; ULA_0[3:0] = out_6; ULA_1[3:0] = out_7; ULA_2[3:0] = out_8; ULA_3[3:0] = out_9
endmodule

module Contador_8bits (
  input  Toggle,
  input  Operando0,
  input  Operando1,
  input  Operando_2,
  input  Operando_3,
  input  CLK,
  input  CLR,
  output S0,
  output S1,
  output S2,
  output S3,
  output S4,
  output S5,
  output S6,
  output S7
);

  wire and_1_out, and_2_out, and_3_out, and_4_out, and_5_out, and_6_out, and_7_out, and_8_out, and_9_out,
       and_10_out, and_11_out, and_12_out, and_13_out, and_14_out, not_1_out, not_2_out, not_3_out,
       not_4_out, or_1_out, or_2_out, or_3_out, or_4_out;

  and and_1 (and_1_out, Toggle, Operando0);
  not not_1 (not_1_out, Operando0);
  T_Flip_Flop t_ff_1 (.clk(CLK), .T(1'b1), .Q(S0), .preset(and_1_out), .reset(or_1_out));  // open: Qn
  or or_1 (or_1_out, and_2_out, CLR);
  and and_2 (and_2_out, not_1_out, Toggle);
  and and_3 (and_3_out, Toggle, Operando1);
  not not_2 (not_2_out, Operando1);
  or or_2 (or_2_out, and_4_out, CLR);
  and and_4 (and_4_out, not_2_out, Toggle);
  T_Flip_Flop t_ff_2 (.clk(CLK), .T(S0), .Q(S1), .preset(and_3_out), .reset(or_2_out));  // open: Qn
  and and_5 (and_5_out, Toggle, Operando_2);
  not not_3 (not_3_out, Operando_2);
  T_Flip_Flop t_ff_3 (.clk(CLK), .T(and_6_out), .Q(S2), .preset(and_5_out), .reset(or_3_out));  // open: Qn
  and and_6 (and_6_out, S1, S0);
  or or_3 (or_3_out, and_7_out, CLR);
  and and_7 (and_7_out, not_3_out, Toggle);
  and and_8 (and_8_out, Toggle, Operando_3);
  not not_4 (not_4_out, Operando_3);
  and and_9 (and_9_out, S2, and_6_out);
  or or_4 (or_4_out, and_10_out, CLR);
  and and_10 (and_10_out, not_4_out, Toggle);
  T_Flip_Flop t_ff_4 (.clk(CLK), .T(and_9_out), .Q(S3), .preset(and_8_out), .reset(or_4_out));  // open: Qn
  T_Flip_Flop t_ff_5 (.clk(CLK), .T(and_11_out), .Q(S4), .reset(CLR));  // open: Qn, preset
  and and_11 (and_11_out, S3, and_9_out);
  and and_12 (and_12_out, S4, and_11_out);
  T_Flip_Flop t_ff_6 (.clk(CLK), .T(and_12_out), .Q(S5), .reset(CLR));  // open: Qn, preset
  T_Flip_Flop t_ff_7 (.clk(CLK), .T(and_13_out), .Q(S6), .reset(CLR));  // open: Qn, preset
  and and_13 (and_13_out, S5, and_12_out);
  and and_14 (and_14_out, S6, and_13_out);
  T_Flip_Flop t_ff_8 (.clk(CLK), .T(and_14_out), .Q(S7), .reset(CLR));  // open: Qn, preset
endmodule

module Contador_de_Memoria (
  input  CLK,
  input  CLR,
  output [1:0] RgTO,
  output [1:0] RgIN,
  output [1:0] JMP,
  output [1:0] ULA,
  output [3:0] \Disponível ,
  output [3:0] Operando,
  output out_9,
  output out_10,
  output out_11,
  output out_12,
  output out_13,
  output out_14,
  output out_15,
  output out_16,
  output ULA_State,
  output Reset_Registers
);

  wire Jump_Toggle, not_1_out, not_2_out, not_3_out, not_4_out, or_1_out, Reset_PC;

  or or_1 (or_1_out, CLR, Reset_PC);
  Contador_8bits contador_8bits_1 (
    .CLK(CLK), .S0(out_9), .S1(out_10), .S2(out_11), .S3(out_12), .S4(out_13), .S5(out_14), .S6(out_15),
    .S7(out_16), .CLR(or_1_out), .Operando0(Operando[0]), .Operando1(Operando[1]), .Operando_2(Operando[2]),
    .Operando_3(Operando[3]), .Toggle(Jump_Toggle));
  not not_1 (not_1_out, JMP[1]);
  not not_2 (not_2_out, JMP[0]);
  not not_3 (not_3_out, JMP[1]);
  not not_4 (not_4_out, JMP[0]);
  and and_1 (ULA_State, not_1_out, not_2_out);
  and and_2 (Reset_Registers, not_3_out, JMP[0]);
  and and_3 (Reset_PC, JMP[1], not_4_out);
  and and_4 (Jump_Toggle, JMP[1], JMP[0]);
  ROM #(.dataWidth(16), .Select("low")) ROM (
    .addr({out_16, out_15, out_14, out_13, out_12, out_11, out_10, out_9}),
    .data({RgTO, RgIN, JMP, ULA, \Disponível , Operando}));

  // Other names for the same wires on the sheet: JMP_IN[1:0] = JMP

  // Notes on the sheet:
  //   contents of ROM (hex, n*v repeats v):
  //   6044 9142 62c1 63c5 9042 6072 90a3 4a0 c0d 4*0 9002 6372 6141 9342 6210 6013 840
endmodule

module Rg_IN_Multiplexer (
  input  [1:0] in_1,
  input  [3:0] in_2,
  input  [3:0] in_3,
  output [3:0] out_4
);

  wire and_1_out, and_2_out, and_3_out, and_4_out, and_5_out, and_6_out, and_7_out, and_8_out, and_9_out,
       and_10_out, not_1_out, not_2_out;

  not not_1 (not_1_out, in_1[1]);
  and and_1 (and_1_out, not_1_out, in_1[0]);
  and and_2 (and_2_out, in_1[1], not_2_out);
  not not_2 (not_2_out, in_1[0]);
  and and_3 (and_3_out, in_2[3], and_1_out);
  and and_4 (and_4_out, in_2[2], and_1_out);
  or or_1 (out_4[2], and_4_out, and_7_out);
  or or_2 (out_4[3], and_3_out, and_8_out);
  and and_5 (and_5_out, in_2[1], and_1_out);
  and and_6 (and_6_out, in_2[0], and_1_out);
  or or_3 (out_4[1], and_5_out, and_9_out);
  or or_4 (out_4[0], and_6_out, and_10_out);
  and and_7 (and_7_out, in_3[2], and_2_out);
  and and_8 (and_8_out, in_3[3], and_2_out);
  and and_9 (and_9_out, in_3[1], and_2_out);
  and and_10 (and_10_out, in_3[0], and_2_out);
endmodule

module RG_To_Multiplexer (
  input  [1:0] in_1,
  input  [3:0] in_2,
  input  [3:0] in_3,
  output [3:0] out_4
);

  wire and_1_out, and_2_out, and_3_out, and_4_out, and_5_out, and_6_out, and_7_p1, and_7_p4, and_7_p6,
       not_1_out, not_2_out;

  not not_1 (not_1_out, in_1[1]);
  and and_1 (and_1_out, not_1_out, in_1[0]);
  and and_2 (and_2_out, in_1[1], not_2_out);
  not not_2 (not_2_out, in_1[0]);
  and and_3 (and_3_out, in_2[2], and_1_out);
  and and_4 (and_4_out, in_2[3], and_1_out);
  and and_5 (and_5_out, in_2[0], and_1_out);
  and and_6 (and_6_out, in_2[1], and_1_out);
  // AND_Gate and_7: pin names not known; wires that end beside it: and_7_p1, in_3[3], and_2_out, and_7_p4, in_3[2], and_7_p6
  // AND_Gate and_8 has open pins: in0=and_7_p6, out=open
  // AND_Gate and_9: pin names not known; wires that end beside it: and_2_out, in_3[0], and_2_out
  // AND_Gate and_10: pin names not known; wires that end beside it: and_2_out, in_3[1], and_2_out, in_3[0]
endmodule

module Music (
  input  [3:0] Disp,
  input  in_2
);

  wire [13:0] adder_1_out, multiplier_1_out;

  Multiplier #(.width(14)) multiplier_1 (
    .a({{10{1'b0}}, Disp}), .b(14'h10), .out(multiplier_1_out));  // open: cin, cout
  Adder #(.width(14)) adder_1 (.a(multiplier_1_out), .b(14'h14a), .out(adder_1_out));  // open: cin, cout
  // Buzzer #(.vol_width(4)) buzzer_1: pin names not known; wires that end beside it: adder_1_out, in_2, 4'b1111

  // Other names for the same wires on the sheet: Music[3:0] = Disp
endmodule
