// Logisim project registradorCargaParalela.circ as structural Verilog: 1 circuit, main circuit main
module main (
  input  in_1,
  input  in_2,
  input  in_3,
  input  in_4,
  input  in_5,
  output out_6,
  output out_7,
  output out_8,
  output out_9
);

  D_Flip_Flop d_ff_1 (.clk(in_1), .D(in_2), .Q(out_6));  // open: Qn, preset, reset
  D_Flip_Flop d_ff_2 (.clk(in_1), .D(in_3), .Q(out_7));  // open: Qn, preset, reset
  D_Flip_Flop d_ff_3 (.clk(in_1), .D(in_4), .Q(out_8));  // open: Qn, preset, reset
  D_Flip_Flop d_ff_4 (.clk(in_1), .D(in_5), .Q(out_9));  // open: Qn, preset, reset
endmodule
